// Logisim project ex4.circ as structural Verilog: 17 circuits, main circuit RotRight
module RotRight (
  input  [15:0] INPUT0,
  input  [3:0] AMOUNT,
  output [15:0] OUTPUT0
);

  rot1 rot1_1 ();  // open: in_1, out_2
  rot2 rot2_1 ();  // open: in_1, out_2
  rot4 rot4_1 ();  // open: in_1, out_2
  rot8 rot8_1 ();  // open: in_1, out_2
  Multiplexer #(.select(4), .width(16)) multiplexer_1 ();  // open: in0, in1, in2, in3, in4, in5, in6, in7, in8, in9, in10, in11, in12, in13, in14, in15, out, sel
endmodule

module rot1 (
  input  [15:0] in_1,
  output [15:0] out_2
);
endmodule

module rot2 (
  input  [15:0] in_1,
  output [15:0] out_2
);


  assign out_2 = {in_1[1:0], in_1[15:2]};
endmodule

module rot4 (
  input  [15:0] in_1,
  output [15:0] out_2
);


  assign out_2 = {in_1[3:0], in_1[15:4]};
endmodule

module rot8 (
  input  [15:0] in_1,
  output [15:0] out_2
);


  assign out_2 = {in_1[7:0], in_1[15:8]};
endmodule

module rot3 (
  input  [15:0] in_1,
  output [15:0] out_2
);


  assign out_2 = {in_1[2:0], in_1[15:3]};
endmodule

module rot5 (
  input  [15:0] in_1,
  output [15:0] out_2
);


  assign out_2 = {in_1[4:0], in_1[15:5]};
endmodule

module rot6 (
  input  [15:0] in_1,
  output [15:0] out_2
);


  assign out_2 = {in_1[5:0], in_1[15:6]};
endmodule

module rot7 (
  input  [15:0] in_1,
  output [15:0] out_2
);


  assign out_2 = {in_1[6:0], in_1[15:7]};
endmodule

module rot9 (
  input  [15:0] in_1,
  output [15:0] out_2
);


  assign out_2 = {in_1[8:0], in_1[15:9]};
endmodule

module rot10 (
  input  [15:0] in_1,
  output [15:0] out_2
);


  assign out_2 = {in_1[9:0], in_1[15:10]};
endmodule

module rot11 (
  input  [15:0] in_1,
  output [15:0] out_2
);


  assign out_2 = {in_1[10:0], in_1[15:11]};
endmodule

module rot12 (
  input  [15:0] in_1,
  output [15:0] out_2
);


  assign out_2 = {in_1[11:0], in_1[15:12]};
endmodule

module rot13 (
  input  [15:0] in_1,
  output [15:0] out_2
);


  assign out_2 = {in_1[12:0], in_1[15:13]};
endmodule

module rot14 (
  input  [15:0] in_1,
  output [15:0] out_2
);


  assign out_2 = {in_1[13:0], in_1[15:14]};
endmodule

module rot15 (
  input  [15:0] in_1,
  output [15:0] out_2
);


  assign out_2 = {in_1[14:0], in_1[15]};
endmodule

module rot16 (
  input  [15:0] in_1,
  output [15:0] out_2
);


  assign out_2 = in_1;
endmodule
