// Logisim project control-logic.circ as structural Verilog: 1 circuit, main circuit control_logic
module control_logic (
  input  [31:0] Instruction,
  input  BrEq,
  input  BrLt,
  output PCSel,
  output RegWEn,
  output [2:0] ImmSel,
  output BrUn,
  output ASel,
  output BSel,
  output [3:0] ALUSel,
  output MemWEn,
  output [1:0] WBSel
);

  wire and_3_out, and_4_out, and_5_out, and_6_out, and_7_out, and_8_out, and_11_out, and_12_out, and_13_out,
       and_14_out, nor_1_out, nor_2_out, nor_3_out, nor_4_out, nor_5_out, nor_6_out, nor_7_out, not_1_out,
       not_2_out, not_3_out, not_4_out, not_5_out, not_6_out, not_7_out, not_8_out, not_9_out, not_10_out,
       not_11_out, not_12_out, not_13_out, not_14_out, or_1_out, or_2_out;
  wire [1:0] adder_1_out, adder_2_out, alu0, and_10_out, bit_extender_2_out, bit_extender_3_out, sra0, sub0;
  wire [3:0] AluNum;
  wire [3:2] not_15_out;
  wire [3:3] not_17_out;
  wire [15:0] rom_1_data;

  ROM #(.addrWidth(6), .dataWidth(16)) rom_1 (.data(rom_1_data));  // open: addr
  nor nor_1 (nor_1_out, Instruction[2], Instruction[3]);
  not not_1 (not_1_out, Instruction[6]);
  nor nor_2 (nor_2_out, Instruction[2], Instruction[3]);
  not not_2 (not_2_out, Instruction[6]);
  and and_1 (ASel, nor_1_out, Instruction[4], not_1_out);
  and and_2 (BSel, nor_2_out, Instruction[4], Instruction[5], not_2_out);
  not not_3 (not_3_out, Instruction[4]);
  not not_4 (not_4_out, Instruction[6]);
  and and_3 (and_3_out, Instruction[4], Instruction[5]);
  not not_5 (not_5_out, Instruction[5]);
  or or_1 (or_1_out, Instruction[5], Instruction[6]);
  and and_4 (and_4_out, not_3_out, Instruction[5], not_4_out);
  not not_6 (not_6_out, or_1_out);
  not not_7 (not_7_out, Instruction[13]);
  or or_2 (or_2_out, Instruction[4], not_6_out);
  and and_5 (and_5_out, Instruction[12], not_7_out, Instruction[14]);
  or or_3 (PCSel, and_4_out, and_3_out, not_5_out);
  or or_4 (RegWEn, Instruction[2], or_2_out);
  nor nor_3 (nor_3_out, Instruction[2], Instruction[3]);
  not not_8 (not_8_out, Instruction[6]);
  nor nor_4 (nor_4_out, Instruction[12], Instruction[13], Instruction[14]);
  assign AluNum = {{1{1'b0}}, Instruction[14:12]};  // Bit_Extender bit_extender_1
  and and_6 (and_6_out, nor_4_out, Instruction[30]);
  and and_7 (and_7_out, and_5_out, Instruction[30]);
  and and_8 (and_8_out, nor_3_out, Instruction[4], not_8_out);
  assign bit_extender_2_out = {{1{1'b0}}, and_6_out};  // Bit_Extender bit_extender_2
  assign bit_extender_3_out = {{1{1'b0}}, and_7_out};  // Bit_Extender bit_extender_3
  assign alu0 = {{1{1'b0}}, and_8_out};  // Bit_Extender bit_extender_4
  assign sub0 = bit_extender_2_out & alu0;  // AND_Gate and_9, 2 bits wide
  assign and_10_out = bit_extender_3_out & alu0;  // AND_Gate and_10, 2 bits wide
  nor nor_5 (nor_5_out, Instruction[2], Instruction[3]);
  not not_9 (not_9_out, Instruction[4]);
  not not_10 (not_10_out, Instruction[6]);
  nor nor_6 (nor_6_out, Instruction[2], Instruction[4]);
  not not_11 (not_11_out, Instruction[4]);
  Shifter #(.width(2)) shifter_1 (.in(and_10_out), .\dist (1'b1), .out(sra0));
  and and_11 (and_11_out, Instruction[2], Instruction[4]);
  and and_12 (and_12_out, nor_5_out, not_9_out, Instruction[5], not_10_out);
  and and_13 (and_13_out, Instruction[2], Instruction[4]);
  and and_14 (and_14_out, nor_6_out, Instruction[5], Instruction[6]);
  and and_15 (ImmSel[2], Instruction[2], not_11_out, Instruction[5], Instruction[6]);
  or or_5 (ImmSel[0], and_11_out, and_12_out);
  or or_6 (ImmSel[1], and_13_out, and_14_out);
  not not_12 (not_12_out, Instruction[2]);
  not not_13 (not_13_out, Instruction[3]);
  not not_14 (not_14_out, Instruction[4]);
  not not_15 (not_15_out[2], AluNum[2]);
  not not_16 (not_15_out[3], AluNum[3]);
  not not_17 (not_17_out[3], AluNum[3]);
  and and_16 (BrUn, not_12_out, not_13_out, not_14_out, Instruction[5], Instruction[6], Instruction[13]);
  Adder #(.width(2)) adder_1 (.a(alu0), .b(sub0), .out(adder_1_out));  // open: cin, cout
  nor nor_7 (nor_7_out, Instruction[2], Instruction[4], Instruction[3], Instruction[6]);
  Multiplexer #(.select(2), .width(4)) multiplexer_1 (
    .in1(AluNum), .in2({not_15_out, AluNum[1:0]}), .in3({not_17_out[3], AluNum[2:0]}), .out(ALUSel),
    .sel(adder_2_out));  // open: in0
  Adder #(.width(2)) adder_2 (.a(adder_1_out), .b(sra0), .out(adder_2_out));  // open: cin, cout
  and and_17 (MemWEn, nor_7_out, Instruction[5]);

  // Other names for the same wires on the sheet: opcode[4:0] = Instruction[6:2]; func3[2:0] = Instruction[14:12];
  //   func7 = Instruction[30]

  // Notes on the sheet:
  //   INPUTS to your circuit
  //   Connect ROM Input here ->
  //   ROM FOR CONTROL LOGIC
  //   DON'T CHANGE THE LOCATIONS OF THE INPUTS AND OUTPUTS!
  //   This is only if you choose to do the ROM option
  //   CONNECT
  //   WIRE
  //   TO
  //   USE
  //   ROM
  //   OUTPUT from your circuit
  //   Reminder: If using ROM, use combinational logic for PCSel
endmodule
