// Logisim project regfile.circ as structural Verilog: 1 circuit, main circuit regfile
module regfile (
  input  [4:0] ReadIndex1,
  input  [4:0] ReadIndex2,
  input  [4:0] WriteIndex,
  input  [31:0] WriteData,
  input  RegWEn,
  input  clk,
  output [31:0] ra,
  output [31:0] sp,
  output [31:0] t0,
  output [31:0] t1,
  output [31:0] t2,
  output [31:0] s0,
  output [31:0] s1,
  output [31:0] a0,
  output [31:0] ReadData1,
  output [31:0] ReadData2
);

  wire W1, W2, W3, W4, W5, W6, W7, W8, W9, W10, W11, W12, W13, W14, W15, W16, W17, W18, W19, W20, W21, W22,
       W23, W24, W25, W26, W27, W28, W29, W30, W31;
  wire [31:0] O0, O3, O4, O11, O12, O13, O14, O15;

  Demultiplexer #(.select(5)) demultiplexer_1 (
    .out1(W1), .out2(W2), .out3(W3), .out4(W4), .out5(W5), .out6(W6), .out7(W7), .out8(W8), .out9(W9),
    .out10(W10), .out11(W11), .out12(W12), .out13(W13), .out14(W14), .out15(W15), .out16(W16), .out17(W17),
    .out18(W18), .out19(W19), .out20(W20), .out21(W21), .out22(W22), .out23(W23), .out24(W24), .out25(W25),
    .out26(W26), .out27(W27), .out28(W28), .out29(W29), .out30(W30), .out31(W31), .in(RegWEn),
    .sel(WriteIndex));  // open: out0
  Register #(.width(32)) register_1 (.D(WriteData), .en(W1), .clk(clk), .Q(ra));  // open: clr
  Register #(.width(32)) register_2 (.Q(O0));  // open: D, en, clk, clr
  Register #(.width(32)) register_3 (.D(WriteData), .en(W2), .clk(clk), .Q(sp));  // open: clr
  Register #(.width(32)) register_4 (.D(WriteData), .en(W5), .clk(clk), .Q(t0));  // open: clr
  Register #(.width(32)) register_5 (.D(WriteData), .en(W6), .clk(clk), .Q(t1));  // open: clr
  Register #(.width(32)) register_6 (.D(WriteData), .en(W7), .clk(clk), .Q(t2));  // open: clr
  Register #(.width(32)) register_7 (.D(WriteData), .en(W8), .clk(clk), .Q(s0));  // open: clr
  Register #(.width(32)) register_8 (.D(WriteData), .en(W9), .clk(clk), .Q(s1));  // open: clr
  Register #(.width(32)) register_9 (.D(WriteData), .en(W10), .clk(clk), .Q(a0));  // open: clr
  Register #(.width(32)) register_10 (.D(WriteData), .en(W11), .clk(clk), .Q(O11));  // open: clr
  Register #(.width(32)) register_11 (.D(WriteData), .en(W12), .clk(clk), .Q(O12));  // open: clr
  Register #(.width(32)) register_12 (.D(WriteData), .en(W13), .clk(clk), .Q(O13));  // open: clr
  Register #(.width(32)) register_13 (.D(WriteData), .en(W14), .clk(clk), .Q(O14));  // open: clr
  Register #(.width(32)) register_14 (.D(WriteData), .en(W3), .clk(clk), .Q(O3));  // open: clr
  Register #(.width(32)) register_15 (.D(WriteData), .en(W4), .clk(clk), .Q(O4));  // open: clr
  Register #(.width(32)) register_16 (.D(WriteData), .en(W21), .clk(clk));  // open: Q, clr
  Register #(.width(32)) register_17 (.D(WriteData), .en(W20), .clk(clk));  // open: Q, clr
  Register #(.width(32)) register_18 (.D(WriteData), .en(W19), .clk(clk));  // open: Q, clr
  Register #(.width(32)) register_19 (.D(WriteData), .clk(clk));  // open: en, Q, clr
  Register #(.width(32)) register_20 (.D(WriteData), .en(W17), .clk(clk));  // open: Q, clr
  Register #(.width(32)) register_21 (.D(WriteData), .en(W16), .clk(clk));  // open: Q, clr
  Register #(.width(32)) register_22 (.D(WriteData), .en(W15), .clk(clk), .Q(O15));  // open: clr
  Register #(.width(32)) register_23 (.D(WriteData), .en(W18), .clk(clk));  // open: Q, clr
  Multiplexer #(.select(5), .width(32)) multiplexer_1 ();  // open: in0, in1, in2, in3, in4, in5, in6, in7, in8, in9, in10, in11, in12, in13, in14, in15, in16, in17, in18, in19, in20, in21, in22, in23, in24, in25, in26, in27, in28, in29, in30, in31, out, sel
  Multiplexer #(.select(5), .width(32)) multiplexer_2 ();  // open: in0, in1, in2, in3, in4, in5, in6, in7, in8, in9, in10, in11, in12, in13, in14, in15, in16, in17, in18, in19, in20, in21, in22, in23, in24, in25, in26, in27, in28, in29, in30, in31, out, sel

  // Notes on the sheet:
  //   INPUTS to your circuit
  //   DON'T CHANGE THE LOCATIONS OF THE INPUTS AND OUTPUTS!
  //   These are DEBUG/TEST outputs from your circuit.
  //   OUTPUTS from your circuit
endmodule
